# Fritzing sketch auto-door-unlocker-schematic (saved by Fritzing 0.9.3b)
breadboards: 1

parts:
  MV1 = MicroView [part_number=MicroView package="16pin wide"]
  J2 = Power Jack [package=power_jack_pth]
  R1 = Resistor [tolerance=±5% resistance=10k package=THT]
  R2 = Resistor [tolerance=±5% resistance=10k package=THT]
  U1 = TRANSISTOR_NPN_2 [package=to-92]
  S1 = Momentary Switch [package=ksa_sealed_tac_switch]
  U2 = TRANSISTOR_NPN_2 [package=to-92]
  J3 = Infrared Proximity Sensor
  hc-sr1 = hc-sr04

nets:
  N1: MV1.A2, J3.Vout
  N2: MV1.A0, R1.Pin_0
  GND: MV1.GND, J2.GND, U1.E, J3.GND, hc-sr1.GND
  N3: MV1.D2, hc-sr1.Trig
  N4: MV1.D3, hc-sr1.Echo
  VCC: MV1.5V, J3.Vcc, hc-sr1.VCC
  N5: MV1.Vin, J2.PWR, R2.Pin_1, U2.C
  N6: R1.Pin_1, U1.B
  N7: R2.Pin_0, U1.C, U2.B
  N8: S1.1, S1.2
  N9: S1.3, S1.4, U2.E

custom parts:
  MicroView: MicroView - Chip-sized Arduino with OLED display.
